# Fritzing sketch Sketch (saved by Fritzing 0.9.3b)
circuit board: 8.46667cm x 5.64444cm
breadboards: 1

parts:
  LED1 = ws2812b [package="smd 2812b"]
  F = RFID-RC522-v2
  LED2 = ws2812b [package="smd 2812b"]
  WeMos_D1_Mini1 = WeMos D1 Mini [part_number=1]

nets:
  VDD: LED1.VDD, F.3.3V, LED2.VDD, WeMos_D1_Mini1.3V3
  VSS: LED1.VSS, F.GND, LED2.VSS, WeMos_D1_Mini1.G
  N1: LED1.DIN, WeMos_D1_Mini1.D2
  N2: F.SDA, WeMos_D1_Mini1.D4
  N3: F.SCK, WeMos_D1_Mini1.D5
  N4: F.MOSI, WeMos_D1_Mini1.D7
  N5: F.MISO, WeMos_D1_Mini1.D6
  N6: F.RST, WeMos_D1_Mini1.D1
  N7: LED2.DIN, WeMos_D1_Mini1.D3

custom parts:
  RFID-RC522-v2: A simple China made RFID-RC522 Reader; do check the pin labels, as this is a MFRC522 based clone.
